// Logisim project CPU_V2.circ as structural Verilog: 1 circuit, main circuit main
module main (
  input  in_1,
  input  MEM_WRITE,
  input  MEM_READ,
  input  PC_COUNT,
  input  in_5,
  input  in_6,
  input  [3:0] in_7,
  input  in_8,
  input  [11:0] in_9,
  input  in_10,
  input  [3:0] in_11,
  input  [3:0] in_12,
  input  in_13,
  output [15:0] out_14
);

  wire CLK, decoder_1_out1, decoder_1_out2, decoder_1_out3, decoder_1_out4, decoder_1_out5, decoder_1_out6,
       decoder_1_out7, decoder_1_out12, decoder_1_out13, decoder_1_out14, decoder_1_out15, decoder_2_out1,
       decoder_2_out2, decoder_2_out3, decoder_2_out4, decoder_2_out5, decoder_2_out6, decoder_2_out7,
       decoder_2_out12, decoder_2_out13, decoder_2_out14, decoder_2_out15, JMPC, main_5_oe, main_6_oe,
       main_7_oe, main_9_oe, main_10_oe, main_11_oe, multiplexer_1_out, multiplexer_2_out, or_1_out, R, W;
  wire [3:0] ALU, multiplexer_6_out, multiplexer_7_out, multiplexer_8_out, register_2_q, register_2_q_2;
  wire [7:0] multiplexer_9_out, rom_2_data, ROM_ADDR;
  wire [11:0] C_BUS_SELECT, multiplexer_3_out;
  wire [15:0] H1_out, H2_out, H3_out, LV_out, main_1_a_bus, main_1_b_bus, main_12_c_bus, MAR_out, MBR_DATA,
       MEM_ADDR, MEM_D_IN, MEM_D_OUT, multiplexer_4_out, PC_d_out, SP_out, TOS_out;
  wire [22:0] register_1_q;
  wire [31:0] rom_1_data;

  Multiplexer #(.disabled(0), .enable("false")) multiplexer_1 (
    .in0(W), .in1(MEM_WRITE), .out(multiplexer_1_out), .sel(in_1));
  Multiplexer #(.disabled(0), .enable("false")) multiplexer_2 (
    .in0(R), .in1(MEM_READ), .out(multiplexer_2_out), .sel(in_1));
  RAM #(.addrWidth(16), .dataWidth(16), .bus("separate")) ram_1 (
    .addr(MEM_ADDR), .din(MEM_D_IN), .data(MEM_D_OUT), .str(multiplexer_1_out), .sel(1'b1), .clk(CLK),
    .ld(1'b1), .clr(1'b0));
  Multiplexer #(.width(12), .disabled(0), .enable("false")) multiplexer_3 (
    .in0(C_BUS_SELECT), .in1(in_9), .out(multiplexer_3_out), .sel(in_10));
  or or_1 (or_1_out, multiplexer_2_out, multiplexer_3_out[10]);
  Multiplexer #(.width(16), .enable("false")) multiplexer_4 (
    .in0(main_12_c_bus), .in1(MEM_D_OUT), .out(multiplexer_4_out), .sel(multiplexer_2_out));
  Clock clock_1 (.out(CLK));
  _16_bit_D_register_main MAR (.Clk(CLK), .OE(1'b1), .WE(multiplexer_3_out[11]), .Out(MAR_out), .In(main_12_c_bus));
  _16_bit_D_register_main MDR (.Clk(CLK), .OE(1'b1), .WE(or_1_out), .Out(MEM_D_IN), .In(multiplexer_4_out));
  PC_module_main PC (.CLK(CLK), .COUNT(JMPC), .WE(multiplexer_3_out[9]), .D_OUT(PC_d_out), .D_IN(main_12_c_bus));
  _16_bit_D_register_main MBR (.Clk(CLK), .OE(1'b1), .WE(1'b1), .Out(MBR_DATA), .In(MEM_D_OUT));
  _16_bit_D_register_main SP (.Clk(CLK), .OE(main_5_oe), .WE(multiplexer_3_out[8]), .Out(SP_out), .In(main_12_c_bus));
  _16_bit_D_register_main LV (.Clk(CLK), .OE(main_6_oe), .WE(multiplexer_3_out[7]), .Out(LV_out), .In(main_12_c_bus));
  _16_bit_D_register_main TOS (.Clk(CLK), .OE(main_7_oe), .WE(multiplexer_3_out[6]), .Out(TOS_out), .In(main_12_c_bus));
  _16_bit_D_register_main H0 (.Clk(CLK), .OE(1'b1), .WE(multiplexer_3_out[3]), .Out(out_14), .In(main_12_c_bus));
  _16_bit_D_register_main H1 (.Clk(CLK), .OE(main_9_oe), .WE(multiplexer_3_out[2]), .Out(H1_out), .In(main_12_c_bus));
  _16_bit_D_register_main H2 (.Clk(CLK), .OE(main_10_oe), .WE(multiplexer_3_out[1]), .Out(H2_out), .In(main_12_c_bus));
  _16_bit_D_register_main H3 (.Clk(CLK), .OE(main_11_oe), .WE(multiplexer_3_out[0]), .Out(H3_out), .In(main_12_c_bus));
  Multiplexer #(.width(16), .enable("false")) multiplexer_5 (
    .in0(PC_d_out), .in1(MAR_out), .out(MEM_ADDR), .sel(multiplexer_1_out));
  BUS_selector_main main_1 (
    .D_IN(MAR_out), .A_EN(decoder_1_out1), .B_EN(decoder_2_out1), .A_BUS(main_1_a_bus), .B_BUS(main_1_b_bus));  // open: OE
  BUS_selector_main main_2 (
    .D_IN(MEM_D_IN), .A_EN(decoder_1_out2), .B_EN(decoder_2_out2), .A_BUS(main_1_a_bus), .B_BUS(main_1_b_bus));  // open: OE
  BUS_selector_main main_3 (
    .D_IN(PC_d_out), .A_EN(decoder_1_out3), .B_EN(decoder_2_out3), .A_BUS(main_1_a_bus), .B_BUS(main_1_b_bus));  // open: OE
  BUS_selector_main main_4 (
    .D_IN(MBR_DATA), .A_EN(decoder_1_out4), .B_EN(decoder_2_out4), .A_BUS(main_1_a_bus), .B_BUS(main_1_b_bus));  // open: OE
  BUS_selector_main main_5 (
    .OE(main_5_oe), .D_IN(SP_out), .A_EN(decoder_1_out5), .B_EN(decoder_2_out5), .A_BUS(main_1_a_bus),
    .B_BUS(main_1_b_bus));
  BUS_selector_main main_6 (
    .OE(main_6_oe), .D_IN(LV_out), .A_EN(decoder_1_out6), .B_EN(decoder_2_out6), .A_BUS(main_1_a_bus),
    .B_BUS(main_1_b_bus));
  BUS_selector_main main_7 (
    .OE(main_7_oe), .D_IN(TOS_out), .A_EN(decoder_1_out7), .B_EN(decoder_2_out7), .A_BUS(main_1_a_bus),
    .B_BUS(main_1_b_bus));
  BUS_selector_main main_8 (
    .D_IN(out_14), .A_EN(decoder_1_out12), .B_EN(decoder_2_out12), .A_BUS(main_1_a_bus), .B_BUS(main_1_b_bus));  // open: OE
  BUS_selector_main main_9 (
    .OE(main_9_oe), .D_IN(H1_out), .A_EN(decoder_1_out13), .B_EN(decoder_2_out13), .A_BUS(main_1_a_bus),
    .B_BUS(main_1_b_bus));
  BUS_selector_main main_10 (
    .OE(main_10_oe), .D_IN(H2_out), .A_EN(decoder_1_out14), .B_EN(decoder_2_out14), .A_BUS(main_1_a_bus),
    .B_BUS(main_1_b_bus));
  BUS_selector_main main_11 (
    .OE(main_11_oe), .D_IN(H3_out), .A_EN(decoder_1_out15), .B_EN(decoder_2_out15), .A_BUS(main_1_a_bus),
    .B_BUS(main_1_b_bus));
  ALU_main main_12 (.A_BUS(main_1_a_bus), .B_BUS(main_1_b_bus), .C_BUS(main_12_c_bus), .INS(multiplexer_6_out));
  Multiplexer #(.width(4), .enable("false")) multiplexer_6 (
    .in0(ALU), .in1(in_12), .out(multiplexer_6_out), .sel(in_13));
  Decoder #(.select(4), .disabled(0), .enable("false")) decoder_1 (
    .out1(decoder_1_out1), .out2(decoder_1_out2), .out3(decoder_1_out3), .out4(decoder_1_out4),
    .out5(decoder_1_out5), .out6(decoder_1_out6), .out7(decoder_1_out7), .out12(decoder_1_out12),
    .out13(decoder_1_out13), .out14(decoder_1_out14), .out15(decoder_1_out15), .sel(multiplexer_7_out));  // open: out0, out8, out9, out10, out11
  Decoder #(.select(4), .disabled(0), .enable("false")) decoder_2 (
    .out1(decoder_2_out1), .out2(decoder_2_out2), .out3(decoder_2_out3), .out4(decoder_2_out4),
    .out5(decoder_2_out5), .out6(decoder_2_out6), .out7(decoder_2_out7), .out12(decoder_2_out12),
    .out13(decoder_2_out13), .out14(decoder_2_out14), .out15(decoder_2_out15), .sel(multiplexer_8_out));  // open: out0, out8, out9, out10, out11
  Multiplexer #(.width(4), .disabled(0), .enable("false")) multiplexer_7 (
    .in0(register_2_q_2), .in1(in_7), .out(multiplexer_7_out), .sel(in_6));
  Multiplexer #(.width(4), .disabled(0), .enable("false")) multiplexer_8 (
    .in0(register_2_q), .in1(in_11), .out(multiplexer_8_out), .sel(in_8));
  Multiplexer #(.width(8), .disabled(0), .enable("false")) multiplexer_9 (
    .in0(ROM_ADDR), .in1({in_5, MBR_DATA[15:9]}), .out(multiplexer_9_out), .sel(JMPC));
  ROM #(.dataWidth(32)) rom_1 (.addr(multiplexer_9_out), .data(rom_1_data), .sel(1'b1));
  Register #(.width(32)) register_1 (
    .D(rom_1_data), .en(1'b1),
    .Q({ROM_ADDR, JMPC, register_1_q[22:21], ALU, register_1_q[16:15], C_BUS_SELECT, W, R, register_1_q[0]}),
    .clk(CLK), .clr(1'b0));
  ROM rom_2 (.addr(multiplexer_9_out), .data(rom_2_data), .sel(1'b1));
  Register register_2 (.D(rom_2_data), .en(1'b1), .Q({register_2_q_2, register_2_q}), .clk(CLK), .clr(1'b0));

  // Notes on the sheet:
  //   A BUS SELECT DECODER
  //   B BUS SELECT DECODER
  //   contents of rom_1 (hex, n*v repeats v):
  //   4*800000 5084002 6880078
  //   contents of rom_2 (hex, n*v repeats v):
  //   4*0 30 20
endmodule
